// Logisim project computer1.circ as structural Verilog: 1 circuit, main circuit main
module main (
);

  wire clock_1_out;
  wire [3:0] register_1_q, rom_1_data;
  wire [7:4] rom_1_data_2;

  Clock clock_1 (.out(clock_1_out));
  Register #(.width(4)) register_1 (.D(rom_1_data), .Q(register_1_q), .clk(clock_1_out));  // open: en, clr
  ROM #(.addrWidth(4)) rom_1 (.addr(register_1_q), .data({rom_1_data_2, rom_1_data}));  // open: sel
  Hex_Digit_Display hex_digit_display_1 (.value(rom_1_data_2));  // open: dp

  // Notes on the sheet:
  //   contents of rom_1 (hex, n*v repeats v):
  //   91 82 73 64 55 46 37 28 19
endmodule
