// Logisim project computer4.circ as structural Verilog: 1 circuit, main circuit main
module main (
);

  wire clock_1_out, comparator_1_lt, controlled_buffer_1_out, not_1_out;
  wire [0:0] and_1_out;
  wire [3:0] adder_2_out, controlled_buffer_2_out, register_2_q, register_3_q, register_4_q, register_5_q,
       register_6_q, register_7_q;
  wire [7:0] adder_1_out, register_1_q, rom_1_data;
  wire [23:8] rom_1_data_2;

  Adder adder_1 (.a(rom_1_data), .b({{7{1'b0}}, and_1_out[0]}), .out(adder_1_out));  // open: cin, cout
  Register register_1 (.D(adder_1_out), .Q(register_1_q), .clk(clock_1_out));  // open: en, clr
  Clock clock_1 (.out(clock_1_out));
  and and_1 (and_1_out[0], rom_1_data_2[23], controlled_buffer_1_out);
  Register #(.width(4)) register_2 (
    .D(controlled_buffer_2_out), .Q(register_2_q), .clk(rom_1_data_2[21]));  // open: en, clr
  Register #(.width(4)) register_3 (
    .D(controlled_buffer_2_out), .Q(register_3_q), .clk(rom_1_data_2[20]));  // open: en, clr
  Comparator #(.width(4), .mode("unsigned")) comparator_1 (
    .a(register_2_q), .b(register_3_q), .lt(comparator_1_lt));  // open: gt, eq
  ROM #(.dataWidth(24)) rom_1 (.addr(register_1_q), .data({rom_1_data_2, rom_1_data}));  // open: sel
  assign controlled_buffer_1_out = rom_1_data_2[22] ? not_1_out : 1'bz;  // Controlled_Buffer controlled_buffer_1
  not not_1 (not_1_out, comparator_1_lt);
  assign controlled_buffer_2_out = rom_1_data_2[12] ? rom_1_data_2[11:8] : 4'bz;  // Controlled_Buffer controlled_buffer_2
  Register #(.width(4)) register_4 (
    .D(controlled_buffer_2_out), .Q(register_4_q), .clk(rom_1_data_2[15]));  // open: en, clr
  Register #(.width(4)) register_5 (
    .D(controlled_buffer_2_out), .Q(register_5_q), .clk(rom_1_data_2[16]));  // open: en, clr
  Register #(.width(4)) register_6 (
    .D(controlled_buffer_2_out), .Q(register_6_q), .clk(rom_1_data_2[18]));  // open: en, clr
  assign controlled_buffer_2_out = rom_1_data_2[14] ? adder_2_out : 4'bz;  // Controlled_Buffer controlled_buffer_3
  Adder #(.width(4)) adder_2 (.a(register_4_q), .b(register_5_q), .out(adder_2_out));  // open: cin, cout
  RAM #(.addrWidth(4), .dataWidth(4)) ram_1 (
    .addr(register_6_q), .data(controlled_buffer_2_out), .clk(rom_1_data_2[19]), .ld(rom_1_data_2[17]));  // open: sel, clr
  Hex_Digit_Display hex_digit_display_1 (.value(register_7_q));  // open: dp
  Register #(.width(4)) register_7 (
    .D(controlled_buffer_2_out), .Q(register_7_q), .clk(rom_1_data_2[13]));  // open: en, clr

  // Notes on the sheet:
  //   contents of rom_1 (hex, n*v repeats v):
  //   1001 41002 1103 81104 1105 41106 1107 81108 1209 4120a 100b 8100c 130d 4130e 110f 81110 1411 41412
  //   1213 81214 1015 41016 20017 28018 1119 4111a 2001b 3001c 101d 4101e 401f 84020 1021 41022 20023
  //   28024 1125 41126 20027 30028 1129 4112a 402b 8402c 122d 4122e 2002f 28030 1331 41332 20033 30034
  //   1235 41236 4037 84038 1239 4123a 2003b 22003c 143d 4143e 2003f 120040 c00041 43 44 14 1145 41146
  //   20047 22048 48
endmodule
