// Logisim project 1-1 电开关演示.circ as structural Verilog: 1 circuit, main circuit main
module main (
);

  wire clock_1_out, switch_1_out_3;

  Clock clock_1 (.out(clock_1_out));
  switch switch_1 (.in_2(clock_1_out), .in_1(1'b1), .out_3(switch_1_out_3));
  LED led_1 (.in(switch_1_out_3));

  // Notes on the sheet:
  //   高电平电源
  //   按钮（其实这是自动开关电源，但在logisim编辑模式下可以当作按钮来使用）
  //   （通过鼠标点击它可以进行高低电平切换。浅绿色为高电平，其他颜色代表低电平）
  //   发光二极管
  //   （红色代表发光，灰色代表不发光）
endmodule
