// Logisim project 1-2 反向电开关演示.circ as structural Verilog: 1 circuit, main circuit main
module main (
);

  wire clock_1_out, invert_switch_1_out_3;

  Clock clock_1 (.out(clock_1_out));
  invert_switch invert_switch_1 (.in_1(1'b1), .out_3(invert_switch_1_out_3), .in_2(clock_1_out));
  LED led_1 (.in(invert_switch_1_out_3));

  // Notes on the sheet:
  //   高电平电源
  //   按钮
  //   发光二极管
endmodule
