// Logisim project 电开关Lib.circ as structural Verilog: 2 circuits, main circuit switch
// 电开关
module switch (
  input  in_1,
  input  in_2,
  output out_3
);

  assign out_3 = in_2 ? in_1 : 1'bz;  // Controlled_Buffer controlled_buffer_1
endmodule

// 反向电开关
module invert_switch (
  input  in_1,
  input  in_2,
  output out_3
);

  wire not_1_out;

  assign out_3 = not_1_out ? in_1 : 1'bz;  // Controlled_Buffer controlled_buffer_1
  not not_1 (not_1_out, in_2);
endmodule
