// Logisim project 3-1 电平触发器演示.circ as structural Verilog: 1 circuit, main circuit main
module main (
);

  wire and_1_out, clock_1_out, clock_2_out, not_1_out, not_2_out, not_3_out, or_1_out, switch_1_out_3;

  Clock clock_1 (.out(clock_1_out));
  switch switch_1 (.in_2(clock_1_out), .in_1(or_1_out), .out_3(switch_1_out_3));
  not not_1 (not_1_out, not_2_out);
  not not_2 (not_2_out, clock_1_out);
  LED led_1 (.in(or_1_out));
  or or_1 (or_1_out, switch_1_out_3, and_1_out);
  and and_1 (and_1_out, not_3_out, clock_2_out);
  not not_3 (not_3_out, not_1_out);
  Clock clock_2 (.out(clock_2_out));

  // Notes on the sheet:
  //   按钮
  //   3个非门增加延时
  //   发光二极管
  //   或门
  //   与门
  //   按钮
endmodule
