// Logisim project 3-2 边沿触发器演示.circ as structural Verilog: 1 circuit, main circuit main
module main (
);

  wire clock_1_out, clock_2_out, d_ff_1_q, d_ff_2_q, not_1_out;

  Clock clock_1 (.out(clock_1_out));
  Clock clock_2 (.out(clock_2_out));
  not not_1 (not_1_out, clock_1_out);
  D_Flip_Flop #(.trigger("low")) d_ff_1 (
    .clk(not_1_out), .D(clock_2_out), .Q(d_ff_1_q));  // open: Qn, preset, en, reset
  D_Flip_Flop #(.trigger("low")) d_ff_2 (.clk(clock_1_out), .D(d_ff_1_q), .Q(d_ff_2_q));  // open: Qn, preset, en, reset
  LED led_1 (.in(d_ff_2_q));

  // Notes on the sheet:
  //   按钮
  //   按钮
  //   非门
  //   上升沿触发器
  //   发光二极管
  //   上升沿触发器
endmodule
