// Logisim project 3-3 自动开关电源降频演示.circ as structural Verilog: 1 circuit, main circuit main
module main (
);

  wire clock_1_out, d_ff_1_q, not_1_out;

  Clock clock_1 (.out(clock_1_out));
  D_Flip_Flop d_ff_1 (.clk(clock_1_out), .D(not_1_out), .Q(d_ff_1_q));  // open: Qn, preset, en, reset
  not not_1 (not_1_out, d_ff_1_q);
  LED led_1 (.in(d_ff_1_q));

  // Notes on the sheet:
  //   自动开关电源
  //   上升沿触发器
  //   非门
  //   发光二极管
endmodule
