// Logisim project RS触发器原理演示.circ as structural Verilog: 1 circuit, main circuit main
module main (
);

  wire clock_1_out, clock_2_out, nand_1_out, nand_2_out;

  Clock clock_1 (.out(clock_1_out));
  LED led_1 (.in(nand_1_out));
  nand nand_1 (nand_1_out, clock_1_out, nand_2_out);
  LED led_2 (.in(nand_2_out));
  nand nand_2 (nand_2_out, nand_1_out, clock_2_out);
  Clock clock_2 (.out(clock_2_out));
endmodule
