// Logisim project 2-1 与门原理演示.circ as structural Verilog: 1 circuit, main circuit main
module main (
);

  wire clock_1_out, clock_2_out, switch_1_out_3, switch_2_out_3;

  Clock clock_1 (.out(clock_1_out));
  switch switch_1 (.in_2(clock_1_out), .in_1(1'b1), .out_3(switch_1_out_3));
  Clock clock_2 (.out(clock_2_out));
  switch switch_2 (.in_2(clock_2_out), .in_1(switch_1_out_3), .out_3(switch_2_out_3));
  LED led_1 (.in(switch_2_out_3));

  // Notes on the sheet:
  //   高电平电源
  //   按钮
  //   按钮
  //   发光二极管
endmodule
