// Logisim project 2-5 或非门原理演示.circ as structural Verilog: 1 circuit, main circuit main
module main (
);

  wire clock_1_out, clock_2_out, not_1_out, or_1_out;

  Clock clock_1 (.out(clock_1_out));
  Clock clock_2 (.out(clock_2_out));
  or or_1 (or_1_out, clock_1_out, clock_2_out);
  not not_1 (not_1_out, or_1_out);
  LED led_1 (.in(not_1_out));

  // Notes on the sheet:
  //   按钮
  //   按钮
  //   或门
  //   非门
  //   发光二极管
endmodule
