// Logisim project 2-6 异或门原理演示.circ as structural Verilog: 1 circuit, main circuit main
module main (
);

  wire and_1_out, clock_1_out, clock_2_out, nand_1_out, or_1_out;

  Clock clock_1 (.out(clock_1_out));
  Clock clock_2 (.out(clock_2_out));
  or or_1 (or_1_out, clock_1_out, clock_2_out);
  nand nand_1 (nand_1_out, clock_1_out, clock_2_out);
  and and_1 (and_1_out, or_1_out, nand_1_out);
  LED led_1 (.in(and_1_out));

  // Notes on the sheet:
  //   按钮
  //   按钮
  //   或门
  //   与非门
  //   与门
  //   发光二极管
endmodule
