// Logisim project computer2.circ as structural Verilog: 1 circuit, main circuit main
module main (
);

  wire clock_1_out;
  wire [3:0] adder_1_out, controlled_buffer_1_out, register_1_q, register_2_q, register_3_q, register_4_q,
       rom_1_data;
  wire [12:4] rom_1_data_2;

  Clock clock_1 (.out(clock_1_out));
  Register #(.width(4)) register_1 (.D(rom_1_data), .Q(register_1_q), .clk(clock_1_out));  // open: en, clr
  ROM #(.addrWidth(4), .dataWidth(13)) rom_1 (.addr(register_1_q), .data({rom_1_data_2, rom_1_data}));  // open: sel
  assign controlled_buffer_1_out = rom_1_data_2[8] ? rom_1_data_2[7:4] : 4'bz;  // Controlled_Buffer controlled_buffer_1
  Register #(.width(4)) register_2 (
    .D(controlled_buffer_1_out), .Q(register_2_q), .clk(rom_1_data_2[11]));  // open: en, clr
  Register #(.width(4)) register_3 (
    .D(controlled_buffer_1_out), .Q(register_3_q), .clk(rom_1_data_2[12]));  // open: en, clr
  Adder #(.width(4)) adder_1 (.a(register_2_q), .b(register_3_q), .out(adder_1_out));  // open: cin, cout
  assign controlled_buffer_1_out = rom_1_data_2[10] ? adder_1_out : 4'bz;  // Controlled_Buffer controlled_buffer_2
  Hex_Digit_Display hex_digit_display_1 (.value(register_4_q));  // open: dp
  Register #(.width(4)) register_4 (
    .D(controlled_buffer_1_out), .Q(register_4_q), .clk(rom_1_data_2[9]));  // open: en, clr

  // Notes on the sheet:
  //   contents of rom_1 (hex, n*v repeats v):
  //   121 922 133 1134 405 600
endmodule
