// Logisim project 4-1 数字译码器演示.circ as structural Verilog: 1 circuit, main circuit main
module main (
);

  wire and_1_out, and_2_out, and_3_out, and_4_out, and_5_out, and_6_out, and_7_out, and_8_out, clock_1_out,
       clock_2_out, clock_3_out, not_1_out, not_2_out, not_3_out, not_4_out, not_5_out, not_6_out, not_7_out,
       not_8_out, not_9_out, not_10_out, not_11_out, not_12_out;

  Clock clock_1 (.out(clock_1_out));
  Clock clock_2 (.out(clock_2_out));
  Clock clock_3 (.out(clock_3_out));
  not not_1 (not_1_out, clock_1_out);
  not not_2 (not_2_out, clock_2_out);
  not not_3 (not_3_out, clock_3_out);
  not not_4 (not_4_out, clock_1_out);
  not not_5 (not_5_out, clock_2_out);
  not not_6 (not_6_out, clock_1_out);
  not not_7 (not_7_out, clock_3_out);
  not not_8 (not_8_out, clock_1_out);
  not not_9 (not_9_out, clock_2_out);
  not not_10 (not_10_out, clock_3_out);
  not not_11 (not_11_out, clock_2_out);
  not not_12 (not_12_out, clock_3_out);
  and and_1 (and_1_out, not_1_out, not_2_out, not_3_out);
  and and_2 (and_2_out, not_4_out, not_5_out, clock_3_out);
  and and_3 (and_3_out, not_6_out, clock_2_out, not_7_out);
  and and_4 (and_4_out, not_8_out, clock_2_out, clock_3_out);
  and and_5 (and_5_out, clock_1_out, not_9_out, not_10_out);
  and and_6 (and_6_out, clock_1_out, not_11_out, clock_3_out);
  and and_7 (and_7_out, clock_1_out, clock_2_out, not_12_out);
  and and_8 (and_8_out, clock_1_out, clock_2_out, clock_3_out);
  LED led_1 (.in(and_1_out));
  LED led_2 (.in(and_2_out));
  LED led_3 (.in(and_3_out));
  LED led_4 (.in(and_4_out));
  LED led_5 (.in(and_5_out));
  LED led_6 (.in(and_6_out));
  LED led_7 (.in(and_7_out));
  LED led_8 (.in(and_8_out));
endmodule
