// Logisim project 4-2 加法器演示 .circ as structural Verilog: 1 circuit, main circuit main
module main (
);

  wire [0:0] rom_1_data, rom_2_data, rom_3_data;
  wire [1:0] rom_4_data;
  wire [2:0] clock_3_out, clock_5_out, clock_7_out;
  wire [2:1] clock_1_out;

  Clock clock_1 (.out(clock_1_out[1]));
  Clock clock_2 (.out(clock_1_out[2]));
  Clock clock_3 (.out(clock_3_out[1]));
  Clock clock_4 (.out(clock_3_out[2]));
  Clock clock_5 (.out(clock_5_out[1]));
  Clock clock_6 (.out(clock_5_out[2]));
  Clock clock_7 (.out(clock_7_out[1]));
  Clock clock_8 (.out(clock_7_out[2]));
  ROM #(.addrWidth(3), .dataWidth(2)) rom_1 (
    .addr({clock_1_out, 1'b0}), .data({clock_3_out[0], rom_1_data[0]}));  // open: sel
  ROM #(.addrWidth(3), .dataWidth(2)) rom_2 (.addr(clock_3_out), .data({clock_5_out[0], rom_2_data[0]}));  // open: sel
  ROM #(.addrWidth(3), .dataWidth(2)) rom_3 (.addr(clock_5_out), .data({clock_7_out[0], rom_3_data[0]}));  // open: sel
  ROM #(.addrWidth(3), .dataWidth(2)) rom_4 (.addr(clock_7_out), .data(rom_4_data));  // open: sel
  Hex_Digit_Display hex_digit_display_1 (.value({rom_4_data[0], rom_3_data[0], rom_2_data[0], rom_1_data[0]}));  // open: dp

  // Notes on the sheet:
  //   contents of rom_1 (hex, n*v repeats v):
  //   0 1 1 2 1 2 2 3
  //   contents of rom_2 (hex, n*v repeats v):
  //   0 1 1 2 1 2 2 3
  //   contents of rom_3 (hex, n*v repeats v):
  //   0 1 1 2 1 2 2 3
  //   contents of rom_4 (hex, n*v repeats v):
  //   0 1 1 2 1 2 2 3
endmodule
