// Logisim project 4-3 比较器演示 .circ as structural Verilog: 1 circuit, main circuit main
module main (
);

  wire adder_1_cout, adder_2_cout, or_1_out;
  wire [3:0] adder_1_out, clock_1_out, clock_5_out, not_1_out;

  Clock clock_1 (.out(clock_1_out[0]));
  Clock clock_2 (.out(clock_1_out[1]));
  Clock clock_3 (.out(clock_1_out[2]));
  Clock clock_4 (.out(clock_1_out[3]));
  Clock clock_5 (.out(clock_5_out[0]));
  Clock clock_6 (.out(clock_5_out[1]));
  Clock clock_7 (.out(clock_5_out[2]));
  Clock clock_8 (.out(clock_5_out[3]));
  assign not_1_out = ~clock_5_out;  // NOT_Gate not_1, 4 bits wide
  Adder #(.width(4)) adder_1 (.a(not_1_out), .b(4'b0001), .out(adder_1_out), .cout(adder_1_cout));  // open: cin
  Adder #(.width(4)) adder_2 (.a(clock_1_out), .b(adder_1_out), .cout(adder_2_cout));  // open: out, cin
  or or_1 (or_1_out, adder_2_cout, adder_1_cout);
  LED led_1 (.in(or_1_out));
endmodule
